# Fritzing sketch Wiring (saved by Fritzing 0.9.3b)

parts:
  Part1 = Lithium Ion Polymer Battery 3.7v 500mAh [part_number=1578]  # not connected
  Part2 = Adafruit TPL5110 Power Timer [part_number="Adafruit #3435"]
  Part3 = Adafruit Micro USB Breakout [part_number="Adafruit #1833"]
  Part4 = Adafruit Pro Trinket LiIon/LiPoly Backpack [part_number="Adafruit #2124"]
  Part5 = Adafruit Circuit Playground Dev Edition [part_number="Adafruit #3000"]

nets:
  N1: Part2.VDD, Part4.VBAT
  GND: Part2.GND, Part3.GND, Part4.GND
  N2: Part2.DONE, Part5.D1/TX
  N3: Part3.VBUS, Part4.VBUS

custom parts:
  Lithium Ion Polymer Battery 3.7v 500mAh: Lithium ion polymer (also known as 'lipo' or 'lipoly') batteries are thin, light and powerful. The output ranges from 4.2V when completely charged to 3.7V. This battery has a capacity of 500mAh for a total of about 1.9 Wh. The batteries come pre-attached with a genuine 2-pin JST-PH connector as shown and include the necessary protection circuitry.
  Adafruit TPL5110 Power Timer: With some development boards, low power usage is an afterthought. Especially when price and usability is the main selling point. So what should you do when its time to turn around and make that project of yours run on a battery or solar? Sure you could try to hot-air that regulator off, or you could jerry-rig a relay. Or, use a 555? Ugh, the options aren't that great. The Adafruit TPL5110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
  Adafruit Micro USB Breakout: Simple but effective - this breakout board has a USB Micro-B connector, with all 5 pins broken out. Great for pairing with a microcontroller with USB support, or adding USB 5V power to a project. We use a micro-AB connector with through-hole shielding pads for an excellent strong connection - it won't rip off by accident! Comes with one fully assembled and tested micro B breakout PCB and a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
  Adafruit Pro Trinket LiIon/LiPoly Backpack: If you have a Pro Trinket you probably know it's the perfect little size for a portable project. This LiPoly backpack makes it really easy to do! Instead of wiring 2 or 3 boards together to make a charging system, this little PCB sits on top of the Pro Trinket and allows a LiPoly/LiIon battery to plug in. When the Pro Trinket USB port is powered, the battery is recharged automatically. Unplug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
  Adafruit Circuit Playground Dev Edition: Would you like to learn electronics, with an all-in-one board that has sensors and LEDs built in? Circuit Playground is here - and it's the best way to practice programming on real hardware with no soldering or sewing required! Circuit Playground features an ATmega32u4 processor, just like our popular Flora. The board's also round and has alligator-clip pads around it so you don't have to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
